// Logisim project combination_lock_multiple_codes.circ as structural Verilog: 1 circuit, main circuit main
module main (
);

  wire and_1_out, and_2_out, dipswitch_1_sw1, dipswitch_1_sw2, dipswitch_1_sw3, not_1_out, not_2_out,
       not_3_out, or_1_out;

  DipSwitch #(.number(3)) dipswitch_1 (.sw1(dipswitch_1_sw1), .sw2(dipswitch_1_sw2), .sw3(dipswitch_1_sw3));
  not not_1 (not_1_out, dipswitch_1_sw1);
  not not_2 (not_2_out, dipswitch_1_sw3);
  not not_3 (not_3_out, dipswitch_1_sw2);
  and and_1 (and_1_out, not_1_out, dipswitch_1_sw2, not_2_out);
  and and_2 (and_2_out, dipswitch_1_sw1, not_3_out, dipswitch_1_sw3);
  or or_1 (or_1_out, and_1_out, and_2_out);
  LED led_1 (.in(or_1_out));

  // Notes on the sheet:
  //   ABC
endmodule
