// Logisim project combinational_divider_and_multiplier.circ as structural Verilog: 1 circuit, main circuit main
module main (
  input  [3:0] X,
  input  [3:0] in_2,
  input  [3:0] in_3,
  input  [3:0] B
);

  wire nor_1_out, subtractor_1_bout, subtractor_2_bout, subtractor_3_bout, subtractor_4_bout;
  wire [3:0] adder_3_out, and_2_out, and_3_out, and_4_out, multiplexer_1_out, multiplexer_2_out,
       multiplexer_3_out, multiplexer_4_out, not_4_out, subtractor_1_out, subtractor_2_out, subtractor_3_out,
       subtractor_4_out;
  wire [3:1] adder_1_out, adder_2_out, adder_3_out_2, and_1_out;
  wire [3:3] adder_1_cout, adder_2_cout;
  wire [7:7] adder_3_cout;

  Hex_Digit_Display hex_digit_display_1 (.value(X));  // open: dp
  Hex_Digit_Display hex_digit_display_2 (.value(in_2));  // open: dp
  Hex_Digit_Display hex_digit_display_3 (.value(in_3));  // open: dp
  Hex_Digit_Display hex_digit_display_4 (.value(B));  // open: dp
  nor nor_1 (nor_1_out, in_2[0], in_2[1], in_2[2], in_2[3]);
  assign {and_1_out, adder_3_out[0]} = {4{B[0]}} & in_3;  // AND_Gate and_1, 4 bits wide
  Multiplexer #(.width(4)) multiplexer_1 (
    .in0({3'b000, X[3]}), .in1(subtractor_1_out), .out(multiplexer_1_out), .sel(not_4_out[3]));
  Subtractor #(.width(4)) subtractor_1 (
    .a({3'b000, X[3]}), .b(in_2), .out(subtractor_1_out), .bout(subtractor_1_bout));  // open: bin
  not not_1 (not_4_out[3], subtractor_1_bout);
  assign and_2_out = {4{B[1]}} & in_3;  // AND_Gate and_2, 4 bits wide
  Adder #(.width(4)) adder_1 (
    .a({1'b0, and_1_out}), .b(and_2_out), .out({adder_1_out, adder_3_out[1]}), .cout(adder_1_cout[3]));  // open: cin
  assign and_3_out = {4{B[2]}} & in_3;  // AND_Gate and_3, 4 bits wide
  Subtractor #(.width(4)) subtractor_2 (
    .a({multiplexer_1_out[2:0], X[2]}), .b(in_2), .out(subtractor_2_out), .bout(subtractor_2_bout));  // open: bin
  not not_2 (not_4_out[2], subtractor_2_bout);
  LED led_1 (.in(nor_1_out));
  assign and_4_out = {4{B[3]}} & in_3;  // AND_Gate and_4, 4 bits wide
  Multiplexer #(.width(4)) multiplexer_2 (
    .in0({multiplexer_1_out[2:0], X[2]}), .in1(subtractor_2_out), .out(multiplexer_2_out), .sel(not_4_out[2]));
  Adder #(.width(4)) adder_2 (
    .a({adder_1_cout[3], adder_1_out}), .b(and_3_out), .out({adder_2_out, adder_3_out[2]}),
    .cout(adder_2_cout[3]));  // open: cin
  Subtractor #(.width(4)) subtractor_3 (
    .a({multiplexer_2_out[2:0], X[1]}), .b(in_2), .out(subtractor_3_out), .bout(subtractor_3_bout));  // open: bin
  not not_3 (not_4_out[1], subtractor_3_bout);
  Adder #(.width(4)) adder_3 (
    .a({adder_2_cout[3], adder_2_out}), .b(and_4_out), .out({adder_3_out_2, adder_3_out[3]}),
    .cout(adder_3_cout[7]));  // open: cin
  Multiplexer #(.width(4)) multiplexer_3 (
    .in0({multiplexer_2_out[2:0], X[1]}), .in1(subtractor_3_out), .out(multiplexer_3_out), .sel(not_4_out[1]));
  Subtractor #(.width(4)) subtractor_4 (
    .a({multiplexer_3_out[2:0], X[0]}), .b(in_2), .out(subtractor_4_out), .bout(subtractor_4_bout));  // open: bin
  Multiplexer #(.width(4)) multiplexer_4 (
    .in0({multiplexer_3_out[2:0], X[0]}), .in1(subtractor_4_out), .out(multiplexer_4_out), .sel(not_4_out[0]));
  not not_4 (not_4_out[0], subtractor_4_bout);
  Hex_Digit_Display hex_digit_display_5 (.value(adder_3_out));  // open: dp
  Hex_Digit_Display hex_digit_display_6 (.value({adder_3_cout[7], adder_3_out_2}));  // open: dp
  Hex_Digit_Display hex_digit_display_7 (.value(multiplexer_4_out));  // open: dp
  Hex_Digit_Display hex_digit_display_8 (.value(not_4_out));  // open: dp

  // Notes on the sheet:
  //   Y
  //   A
  //   Dividend
  //   Divisor
  //   Combinational divider (4 bit dividend, 4 bit divisor)
  //   Division by zero
  //   Combinational multiplier (4 bit A, 4 bit B, 8 bits A*B)
  //   Remainder
  //   Result (quotient)
endmodule
