// Logisim project demultiplexer.circ as structural Verilog: 1 circuit, main circuit main
module main (
  input  Select,
  input  in_2,
  input  in_3,
  input  in_4,
  input  in_5,
  input  in_6,
  input  Input,
  input  in_8
);

  wire and_1_out, and_2_out, and_3_out, and_4_out, and_5_out, and_6_out, and_7_out, and_8_out, and_9_out,
       and_10_out, and_11_out, and_12_out, and_13_out, and_14_out, demultiplexer_1_out0,
       demultiplexer_1_out1, demultiplexer_1_out2, demultiplexer_1_out3, demultiplexer_1_out4,
       demultiplexer_1_out5, demultiplexer_1_out6, demultiplexer_1_out7;

  and and_1 (and_1_out, in_8, ~in_6);  // AND_Gate
  and and_2 (and_2_out, in_8, in_6);
  and and_3 (and_3_out, and_1_out, ~in_5);  // AND_Gate
  and and_4 (and_4_out, and_1_out, in_5);
  and and_5 (and_5_out, and_2_out, ~in_5);  // AND_Gate
  and and_6 (and_6_out, and_2_out, in_5);
  and and_7 (and_7_out, and_3_out, ~in_2);  // AND_Gate
  and and_8 (and_8_out, and_3_out, in_2);
  and and_9 (and_9_out, and_4_out, ~in_2);  // AND_Gate
  and and_10 (and_10_out, and_4_out, in_2);
  and and_11 (and_11_out, and_5_out, ~in_2);  // AND_Gate
  and and_12 (and_12_out, and_5_out, in_2);
  and and_13 (and_13_out, and_6_out, ~in_2);  // AND_Gate
  and and_14 (and_14_out, and_6_out, in_2);
  LED led_1 (.in(and_7_out));
  LED led_2 (.in(and_8_out));
  LED led_3 (.in(and_9_out));
  LED led_4 (.in(and_10_out));
  LED led_5 (.in(and_11_out));
  LED led_6 (.in(and_12_out));
  LED led_7 (.in(and_13_out));
  LED led_8 (.in(and_14_out));
  Demultiplexer #(.select(3)) demultiplexer_1 (
    .out0(demultiplexer_1_out0), .out1(demultiplexer_1_out1), .out2(demultiplexer_1_out2),
    .out3(demultiplexer_1_out3), .out4(demultiplexer_1_out4), .out5(demultiplexer_1_out5),
    .out6(demultiplexer_1_out6), .out7(demultiplexer_1_out7), .in(Input), .sel({in_4, in_3, Select}));
  LED led_9 (.in(demultiplexer_1_out0));
  LED led_10 (.in(demultiplexer_1_out1));
  LED led_11 (.in(demultiplexer_1_out2));
  LED led_12 (.in(demultiplexer_1_out3));
  LED led_13 (.in(demultiplexer_1_out4));
  LED led_14 (.in(demultiplexer_1_out5));
  LED led_15 (.in(demultiplexer_1_out6));
  LED led_16 (.in(demultiplexer_1_out7));

  // Notes on the sheet:
  //   Input
  //   Select
  //   8-channel demultiplexer
  //   Outputs
  //   Outputs
endmodule
