// Logisim project flip_flops.circ as structural Verilog: 1 circuit, main circuit main
module main (
  input  R,
  input  S,
  input  CLK,
  input  S_2,
  input  R_2,
  input  CLK_2,
  input  in_7,
  input  CLK_3,
  input  in_9,
  input  J,
  input  CLK_4,
  input  CLK_5,
  input  D,
  input  K,
  input  CLK_6,
  input  T
);

  wire and_1_out, and_2_out, and_3_out, and_4_out, button_1_out, button_2_out, button_3_out, button_4_out,
       button_5_out, button_6_out, button_7_out, button_8_out, d_ff_1_q, d_ff_1_qn, j_k_ff_1_q, j_k_ff_1_qn,
       nand_1_out, nand_2_out, nand_3_out, nand_4_out, nand_5_out, nand_6_out, nand_7_out, nand_8_out,
       nor_1_out, nor_2_out, nor_3_out, nor_4_out, not_1_out, not_2_out, not_3_out, not_4_out, s_r_ff_1_q,
       s_r_ff_1_qn, t_ff_1_q, t_ff_1_qn;

  not not_1 (not_1_out, CLK);
  not not_2 (not_2_out, CLK_2);
  D_Flip_Flop d_ff_1 (.clk(CLK_4), .D(D), .Q(d_ff_1_q), .Qn(d_ff_1_qn), .preset(button_1_out), .reset(button_2_out));
  Button button_1 (.out(button_1_out));
  Button button_2 (.out(button_2_out));
  and and_1 (and_1_out, R, not_1_out);
  and and_2 (and_2_out, not_1_out, S);
  LED led_1 (.in(d_ff_1_q));
  LED led_2 (.in(d_ff_1_qn));
  nand nand_1 (nand_1_out, S_2, not_2_out);
  nand nand_2 (nand_2_out, not_2_out, R_2);
  nor nor_1 (nor_1_out, and_1_out, nor_2_out);
  nor nor_2 (nor_2_out, nor_1_out, and_2_out);
  not not_3 (not_3_out, not_1_out);
  nand nand_3 (nand_3_out, nand_1_out, nand_4_out);
  nand nand_4 (nand_4_out, nand_3_out, nand_2_out);
  not not_4 (not_4_out, not_2_out);
  Button button_3 (.out(button_3_out));
  T_Flip_Flop t_ff_1 (.clk(CLK_6), .T(T), .Q(t_ff_1_q), .Qn(t_ff_1_qn), .preset(button_4_out), .reset(button_5_out));
  Button button_4 (.out(button_4_out));
  Button button_5 (.out(button_5_out));
  S_R_Flip_Flop s_r_ff_1 (
    .S(in_7), .clk(CLK_3), .R(in_9), .Q(s_r_ff_1_q), .Qn(s_r_ff_1_qn), .preset(button_3_out),
    .reset(button_6_out));
  LED led_3 (.in(s_r_ff_1_q));
  LED led_4 (.in(s_r_ff_1_qn));
  Button button_6 (.out(button_6_out));
  LED led_5 (.in(t_ff_1_q));
  LED led_6 (.in(t_ff_1_qn));
  and and_3 (and_3_out, nor_2_out, not_3_out);
  and and_4 (and_4_out, not_3_out, nor_1_out);
  nand nand_5 (nand_5_out, nand_3_out, not_4_out);
  nand nand_6 (nand_6_out, not_4_out, nand_4_out);
  J_K_Flip_Flop j_k_ff_1 (
    .J(J), .clk(CLK_5), .K(K), .Q(j_k_ff_1_q), .Qn(j_k_ff_1_qn), .preset(button_7_out), .reset(button_8_out));
  Button button_7 (.out(button_7_out));
  Button button_8 (.out(button_8_out));
  nor nor_3 (nor_3_out, and_3_out, nor_4_out);
  LED led_7 (.in(nor_3_out));
  nor nor_4 (nor_4_out, nor_3_out, and_4_out);
  LED led_8 (.in(nor_4_out));
  nand nand_7 (nand_7_out, nand_5_out, nand_8_out);
  nand nand_8 (nand_8_out, nand_7_out, nand_6_out);
  LED led_9 (.in(j_k_ff_1_q));
  LED led_10 (.in(j_k_ff_1_qn));
  LED led_11 (.in(nand_7_out));
  LED led_12 (.in(nand_8_out));

  // Notes on the sheet:
  //   S
  //   R
  //   E
  //   S
  //   E
  //   R
  //   D flip-flop with asynchronous Set and Reset
  //   S
  //   R
  //   asynchronous
  //   synchronous S
  //   synchronous R
  //   Q
  //   NOT(Q)
  //   Q
  //   NOT(Q)
  //   SR flip-flop with additional asynchronous Set and Reset
  //   S
  //   asynchronous
  //   T flip-flop with asynchronous Set and Reset
  //   S
  //   R
  //   asynchronous
  //   positive edge-triggered SR flip-flop (master-slave design)
  //   R
  //   E
  //   S
  //   positive edge-triggered SR flip-flop using NAND gates (master-slave design)
  //   S
  //   NOT(Q)
  //   E
  //   Q
  //   R
  //   R
  //   Q
  //   Q
  //   NOT(Q)
  //   S
  //   NOT(Q)
  //   JK flip-flop with asynchronous Set and Reset
  //   R
  //   asynchronous
  //   Q
  //   NOT(Q)
  //   Q
  //   NOT(Q)
  //   Q
  //   NOT(Q)
endmodule
