// Logisim project fsm_example.circ as structural Verilog: 1 circuit, main circuit main
module main (
);

  wire clock_1_out, D0_q, D0_qn, D1_q, or_1_out, por_1_out, xor_1_out;

  POR por_1 (.out(por_1_out));
  Clock clock_1 (.out(clock_1_out));
  D_Flip_Flop D0 (.D(D0_qn), .clk(clock_1_out), .Q(D0_q), .Qn(D0_qn), .reset(por_1_out));  // open: preset
  D_Flip_Flop D1 (.D(xor_1_out), .clk(clock_1_out), .Q(D1_q), .reset(por_1_out));  // open: Qn, preset
  xor xor_1 (xor_1_out, D0_q, D1_q);
  or or_1 (or_1_out, D0_qn, D1_q);
  LED led_1 (.in(or_1_out));
  LED led_2 (.in(D0_q));
  LED led_3 (.in(D1_q));

  // Notes on the sheet:
  //   O0
  //   O1
  //   O2
endmodule
