// Logisim project hex_code_printer.circ as structural Verilog: 1 circuit, main circuit main
module main (
);

  wire and_1_out, blank_sel, clock_1_out, clock_2_out, clock_3_out, clock_4_out, clock_5_out, d_ff_1_qn,
       d_ff_2_q, d_ff_2_qn, or_1_out, por_1_out, rdy, read, sel_nibble, wr_en, xor_1_out;
  wire [3:0] multiplexer_1_out;
  wire [6:0] keyboard_1_data;
  wire [7:0] bit_extender_1_out, multiplexer_2_out, register_1_q, rom_1_data;

  Clock clock_1 (.out(clock_1_out));
  Keyboard keyboard_1 (.clk(clock_1_out), .re(read), .avail(rdy), .data(keyboard_1_data));  // open: clr
  POR por_1 (.out(por_1_out));
  or or_1 (or_1_out, d_ff_2_q, rdy);
  Register register_1 (.D(bit_extender_1_out), .en(read), .clk(clock_2_out), .Q(register_1_q));  // open: clr
  assign bit_extender_1_out = {{1{1'b0}}, keyboard_1_data};  // Bit_Extender bit_extender_1
  Clock clock_2 (.out(clock_2_out));
  D_Flip_Flop d_ff_1 (
    .D(and_1_out), .clk(clock_3_out), .Q(sel_nibble), .Qn(d_ff_1_qn), .reset(por_1_out));  // open: preset
  and and_1 (and_1_out, or_1_out, d_ff_1_qn);
  Clock clock_3 (.out(clock_3_out));
  D_Flip_Flop d_ff_2 (
    .D(xor_1_out), .clk(clock_4_out), .Q(d_ff_2_q), .Qn(d_ff_2_qn), .reset(por_1_out));  // open: preset
  Clock clock_4 (.out(clock_4_out));
  Multiplexer #(.width(4)) multiplexer_1 (
    .in0(register_1_q[3:0]), .in1(register_1_q[7:4]), .out(multiplexer_1_out), .sel(sel_nibble));
  xor xor_1 (xor_1_out, sel_nibble, d_ff_2_q);
  and and_2 (read, d_ff_1_qn, d_ff_2_qn, rdy);
  ROM #(.addrWidth(4)) rom_1 (.addr(multiplexer_1_out), .data(rom_1_data));
  or or_2 (wr_en, sel_nibble, d_ff_2_q);
  and and_3 (blank_sel, d_ff_2_q, sel_nibble);
  Multiplexer #(.width(8)) multiplexer_2 (.in0(rom_1_data), .in1(8'h20), .out(multiplexer_2_out), .sel(blank_sel));
  Clock clock_5 (.out(clock_5_out));
  TTY tty_1 (.data(multiplexer_2_out[6:0]), .clk(clock_5_out), .we(wr_en));  // open: clr

  // Notes on the sheet:
  //   contents of rom_1 (hex, n*v repeats v):
  //   30 31 32 33 34 35 36 37 38 39 41 42 43 44 45 46
endmodule
