// Logisim project latches.circ as structural Verilog: 1 circuit, main circuit main
module main (
  input  D,
  input  E__Enable,
  input  D_2,
  input  E__Enable_2
);

  wire and_1_out, and_2_out, and_3_out, and_4_out, button_1_out, button_2_out, button_3_out, button_4_out,
       button_5_out, button_6_out, button_7_out, button_8_out, button_9_out, button_10_out, nand_1_out,
       nand_2_out, nand_3_out, nand_4_out, nand_5_out, nand_6_out, nand_7_out, nand_8_out, nand_9_out,
       nand_10_out, nor_1_out, nor_2_out, nor_3_out, nor_4_out, nor_5_out, nor_6_out, not_1_out, not_2_out;

  Button button_1 (.out(button_1_out));
  Button button_2 (.out(button_2_out));
  Button button_3 (.out(button_3_out));
  Button button_4 (.out(button_4_out));
  Button button_5 (.out(button_5_out));
  Button button_6 (.out(button_6_out));
  and and_1 (and_1_out, button_1_out, E__Enable);
  and and_2 (and_2_out, E__Enable, button_2_out);
  nor nor_1 (nor_1_out, button_5_out, nor_2_out);
  nor nor_2 (nor_2_out, nor_1_out, button_6_out);
  nand nand_1 (nand_1_out, button_3_out, E__Enable_2);
  nand nand_2 (nand_2_out, E__Enable_2, button_4_out);
  LED led_1 (.in(nor_1_out));
  LED led_2 (.in(nor_2_out));
  nor nor_3 (nor_3_out, and_1_out, nor_4_out);
  LED led_3 (.in(nor_3_out));
  nor nor_4 (nor_4_out, nor_3_out, and_2_out);
  LED led_4 (.in(nor_4_out));
  nand nand_3 (nand_3_out, nand_1_out, nand_4_out);
  nand nand_4 (nand_4_out, nand_3_out, nand_2_out);
  LED led_5 (.in(nand_3_out));
  LED led_6 (.in(nand_4_out));
  Button button_7 (.out(button_7_out));
  not not_1 (not_1_out, D_2);
  Button button_8 (.out(button_8_out));
  Button #(.press("passive")) button_9 (.out(button_9_out));
  Button #(.press("passive")) button_10 (.out(button_10_out));
  not not_2 (not_2_out, D);
  nand nand_5 (nand_5_out, button_9_out, nand_6_out);
  nand nand_6 (nand_6_out, nand_5_out, button_10_out);
  and and_3 (and_3_out, not_2_out, button_7_out);
  and and_4 (and_4_out, button_7_out, D);
  nand nand_7 (nand_7_out, D_2, button_8_out);
  nand nand_8 (nand_8_out, button_8_out, not_1_out);
  LED led_7 (.in(nand_5_out));
  LED led_8 (.in(nand_6_out));
  nor nor_5 (nor_5_out, and_3_out, nor_6_out);
  nor nor_6 (nor_6_out, nor_5_out, and_4_out);
  nand nand_9 (nand_9_out, nand_7_out, nand_10_out);
  nand nand_10 (nand_10_out, nand_9_out, nand_8_out);
  LED led_9 (.in(nor_5_out));
  LED led_10 (.in(nor_6_out));
  LED led_11 (.in(nand_9_out));
  LED led_12 (.in(nand_10_out));

  // Notes on the sheet:
  //   R
  //   S
  //   R
  //   S
  //   S
  //   R
  //   SR NOR latch
  //   Gated SR latch
  //   Gated SR latch using NAND gates
  //   Q
  //   NOT(Q)
  //   Q
  //   NOT(Q)
  //   Q
  //   NOT(Q)
  //   Asynchronous latches
  //   E (Enable)
  //   E (Enable)
  //   Neg S
  //   Neg R
  //   Neg S Neg R NAND latch
  //   Gated D latch
  //   Gated D latch using NAND gates
  //   Q
  //   NOT(Q)
  //   Q
  //   Q
  //   NOT(Q)
  //   NOT(Q)
endmodule
