// Logisim project multiplexer.circ as structural Verilog: 1 circuit, main circuit main
module main (
  input  Select,
  input  in_2,
  input  in_3,
  input  in_4,
  input  in_5,
  input  in_6,
  input  in_7,
  input  in_8,
  input  in_9,
  input  in_10,
  input  in_11,
  input  in_12,
  input  in_13,
  input  in_14,
  input  in_15,
  input  in_16,
  input  in_17,
  input  in_18,
  input  in_19,
  input  in_20,
  input  in_21,
  input  in_22
);

  wire and_1_out, and_2_out, and_3_out, and_4_out, and_5_out, and_6_out, and_7_out, and_8_out, and_9_out,
       and_10_out, and_11_out, and_12_out, and_13_out, and_14_out, multiplexer_1_out, or_1_out, or_2_out,
       or_3_out, or_4_out, or_5_out, or_6_out, or_7_out;

  and and_1 (and_1_out, in_15, ~in_4);  // AND_Gate
  or or_1 (or_1_out, and_1_out, and_2_out);
  and and_2 (and_2_out, in_16, in_4);
  and and_3 (and_3_out, in_17, ~in_4);  // AND_Gate
  or or_2 (or_2_out, and_3_out, and_4_out);
  and and_4 (and_4_out, in_18, in_4);
  and and_5 (and_5_out, in_19, ~in_4);  // AND_Gate
  or or_3 (or_3_out, and_5_out, and_6_out);
  and and_6 (and_6_out, in_20, in_4);
  and and_7 (and_7_out, in_21, ~in_4);  // AND_Gate
  or or_4 (or_4_out, and_7_out, and_8_out);
  and and_8 (and_8_out, in_22, in_4);
  and and_9 (and_9_out, or_1_out, ~in_5);  // AND_Gate
  and and_10 (and_10_out, or_2_out, in_5);
  and and_11 (and_11_out, or_3_out, ~in_5);  // AND_Gate
  and and_12 (and_12_out, or_4_out, in_5);
  or or_5 (or_5_out, and_9_out, and_10_out);
  or or_6 (or_6_out, and_11_out, and_12_out);
  and and_13 (and_13_out, or_5_out, ~in_9);  // AND_Gate
  and and_14 (and_14_out, or_6_out, in_9);
  or or_7 (or_7_out, and_13_out, and_14_out);
  LED led_1 (.in(or_7_out));
  Multiplexer #(.select(3)) multiplexer_1 (
    .in0(in_6), .in1(in_7), .in2(in_8), .in3(in_10), .in4(in_11), .in5(in_12), .in6(in_13), .in7(in_14),
    .out(multiplexer_1_out), .sel({in_3, in_2, Select}));
  LED led_2 (.in(multiplexer_1_out));

  // Notes on the sheet:
  //   Inputs
  //   Select
  //   8-channel multiplexer
  //   Inputs
  //   Output
  //   Output
endmodule
