// Logisim project nand_rom.circ as structural Verilog: 1 circuit, main circuit main
module main (
  input  in_1,
  input  in_2,
  input  in_3,
  input  in_4,
  input  in_5,
  input  in_6
);

  wire and_1_out, and_2_out, and_3_out, and_4_out, nand_1_out, nand_2_out, nand_3_out, nand_4_out,
       nand_5_out, nand_6_out, nand_7_out, nand_8_out, not_1_out, transistor_2_out, transistor_3_out,
       transistor_4_out, transistor_5_out, transistor_6_out, transistor_7_out, transistor_8_out,
       transistor_11_out, transistor_12_out, transistor_13_out, transistor_15_out, transistor_16_out,
       transistor_17_out, transistor_18_out, transistor_19_out, transistor_20_out, transistor_21_out,
       transistor_22_out, transistor_23_out, transistor_24_out, transistor_26_out, transistor_27_out,
       transistor_28_out, transistor_29_out, transistor_30_out, transistor_31_out, transistor_32_out,
       transistor_34_out, transistor_35_out, transistor_36_out, transistor_37_out, transistor_38_out,
       transistor_39_out, transistor_40_out, transistor_42_out, transistor_43_out, transistor_44_out,
       transistor_45_out, transistor_46_out, transistor_47_out, transistor_48_out, transistor_50_out,
       transistor_51_out, transistor_52_out, transistor_53_out, transistor_54_out, transistor_55_out,
       transistor_56_out, transistor_58_out, transistor_59_out, transistor_60_out, transistor_61_out,
       transistor_62_out, transistor_63_out, transistor_64_out;
  wire [3:0] pull_resistor_4_node, pull_resistor_8_node, rom_1_data, rom_1_data_2;

  not not_1 (not_1_out, in_3);
  and and_1 (and_1_out, not_1_out, ~in_2);  // AND_Gate
  and and_2 (and_2_out, not_1_out, in_2);
  and and_3 (and_3_out, in_3, ~in_2);  // AND_Gate
  and and_4 (and_4_out, in_3, in_2);
  nand nand_1 (nand_1_out, and_1_out, ~in_1);  // NAND_Gate
  nand nand_2 (nand_2_out, and_1_out, in_1);
  nand nand_3 (nand_3_out, and_2_out, ~in_1);  // NAND_Gate
  nand nand_4 (nand_4_out, and_2_out, in_1);
  nand nand_5 (nand_5_out, and_3_out, ~in_1);  // NAND_Gate
  nand nand_6 (nand_6_out, and_3_out, in_1);
  nand nand_7 (nand_7_out, and_4_out, ~in_1);  // NAND_Gate
  nand nand_8 (nand_8_out, and_4_out, in_1);
  Pull_Resistor #(.pull(1)) pull_resistor_1 (.node(pull_resistor_4_node[3]));
  Transistor #(.\type ("n")) transistor_1 (.in(transistor_2_out), .out(pull_resistor_4_node[3]), .gate(nand_1_out));
  Transistor #(.\type ("n")) transistor_2 (.in(transistor_3_out), .out(transistor_2_out), .gate(nand_2_out));
  Transistor #(.\type ("n")) transistor_3 (.in(transistor_4_out), .out(transistor_3_out), .gate(nand_3_out));
  Transistor #(.\type ("n")) transistor_4 (.in(transistor_5_out), .out(transistor_4_out), .gate(nand_4_out));
  Transistor #(.\type ("n")) transistor_5 (.in(transistor_6_out), .out(transistor_5_out), .gate(nand_5_out));
  Transistor #(.\type ("n")) transistor_6 (.in(transistor_7_out), .out(transistor_6_out), .gate(nand_6_out));
  Transistor #(.\type ("n")) transistor_7 (.in(transistor_8_out), .out(transistor_7_out), .gate(nand_7_out));
  Transistor #(.\type ("n")) transistor_8 (.in(1'b0), .out(transistor_8_out), .gate(nand_8_out));
  Pull_Resistor #(.pull(1)) pull_resistor_2 (.node(pull_resistor_4_node[2]));
  Pull_Resistor #(.pull(1)) pull_resistor_3 (.node(pull_resistor_4_node[1]));
  Transistor #(.\type ("n")) transistor_9 (.in(transistor_11_out), .out(pull_resistor_4_node[2]), .gate(nand_1_out));
  Transistor #(.\type ("n")) transistor_10 (.in(transistor_12_out), .out(pull_resistor_4_node[1]), .gate(nand_1_out));
  Transistor #(.\type ("n")) transistor_11 (.in(transistor_13_out), .out(transistor_11_out), .gate(nand_2_out));
  Transistor #(.\type ("n")) transistor_12 (.in(transistor_12_out), .out(transistor_12_out), .gate(nand_2_out));
  Transistor #(.\type ("n")) transistor_13 (.in(transistor_15_out), .out(transistor_13_out), .gate(nand_3_out));
  Transistor #(.\type ("n")) transistor_14 (.in(transistor_16_out), .out(transistor_12_out), .gate(nand_3_out));
  Transistor #(.\type ("n")) transistor_15 (.in(transistor_17_out), .out(transistor_15_out), .gate(nand_4_out));
  Transistor #(.\type ("n")) transistor_16 (.in(transistor_18_out), .out(transistor_16_out), .gate(nand_4_out));
  Transistor #(.\type ("n")) transistor_17 (.in(transistor_19_out), .out(transistor_17_out), .gate(nand_5_out));
  Transistor #(.\type ("n")) transistor_18 (.in(transistor_20_out), .out(transistor_18_out), .gate(nand_5_out));
  Transistor #(.\type ("n")) transistor_19 (.in(transistor_21_out), .out(transistor_19_out), .gate(nand_6_out));
  Transistor #(.\type ("n")) transistor_20 (.in(transistor_22_out), .out(transistor_20_out), .gate(nand_6_out));
  Transistor #(.\type ("n")) transistor_21 (.in(transistor_23_out), .out(transistor_21_out), .gate(nand_7_out));
  Transistor #(.\type ("n")) transistor_22 (.in(transistor_24_out), .out(transistor_22_out), .gate(nand_7_out));
  Transistor #(.\type ("n")) transistor_23 (.in(1'b0), .out(transistor_23_out), .gate(nand_8_out));
  Transistor #(.\type ("n")) transistor_24 (.in(1'b0), .out(transistor_24_out), .gate(nand_8_out));
  ROM #(.addrWidth(3)) rom_1 (.addr({in_6, in_5, in_4}), .data({rom_1_data_2, rom_1_data}));
  Pull_Resistor #(.pull(1)) pull_resistor_4 (.node(pull_resistor_4_node[0]));
  Transistor #(.\type ("n")) transistor_25 (.in(transistor_26_out), .out(pull_resistor_4_node[0]), .gate(nand_1_out));
  Transistor #(.\type ("n")) transistor_26 (.in(transistor_27_out), .out(transistor_26_out), .gate(nand_2_out));
  Transistor #(.\type ("n")) transistor_27 (.in(transistor_28_out), .out(transistor_27_out), .gate(nand_3_out));
  Transistor #(.\type ("n")) transistor_28 (.in(transistor_29_out), .out(transistor_28_out), .gate(nand_4_out));
  Transistor #(.\type ("n")) transistor_29 (.in(transistor_30_out), .out(transistor_29_out), .gate(nand_5_out));
  Transistor #(.\type ("n")) transistor_30 (.in(transistor_31_out), .out(transistor_30_out), .gate(nand_6_out));
  Transistor #(.\type ("n")) transistor_31 (.in(transistor_32_out), .out(transistor_31_out), .gate(nand_7_out));
  Transistor #(.\type ("n")) transistor_32 (.in(1'b0), .out(transistor_32_out), .gate(nand_8_out));
  Pull_Resistor #(.pull(1)) pull_resistor_5 (.node(pull_resistor_8_node[3]));
  Transistor #(.\type ("n")) transistor_33 (.in(transistor_34_out), .out(pull_resistor_8_node[3]), .gate(nand_1_out));
  Transistor #(.\type ("n")) transistor_34 (.in(transistor_35_out), .out(transistor_34_out), .gate(nand_2_out));
  Transistor #(.\type ("n")) transistor_35 (.in(transistor_36_out), .out(transistor_35_out), .gate(nand_3_out));
  Transistor #(.\type ("n")) transistor_36 (.in(transistor_37_out), .out(transistor_36_out), .gate(nand_4_out));
  Transistor #(.\type ("n")) transistor_37 (.in(transistor_38_out), .out(transistor_37_out), .gate(nand_5_out));
  Transistor #(.\type ("n")) transistor_38 (.in(transistor_39_out), .out(transistor_38_out), .gate(nand_6_out));
  Transistor #(.\type ("n")) transistor_39 (.in(transistor_40_out), .out(transistor_39_out), .gate(nand_7_out));
  Transistor #(.\type ("n")) transistor_40 (.in(1'b0), .out(transistor_40_out), .gate(nand_8_out));
  Pull_Resistor #(.pull(1)) pull_resistor_6 (.node(pull_resistor_8_node[2]));
  Transistor #(.\type ("n")) transistor_41 (.in(transistor_42_out), .out(pull_resistor_8_node[2]), .gate(nand_1_out));
  Transistor #(.\type ("n")) transistor_42 (.in(transistor_43_out), .out(transistor_42_out), .gate(nand_2_out));
  Transistor #(.\type ("n")) transistor_43 (.in(transistor_44_out), .out(transistor_43_out), .gate(nand_3_out));
  Transistor #(.\type ("n")) transistor_44 (.in(transistor_45_out), .out(transistor_44_out), .gate(nand_4_out));
  Transistor #(.\type ("n")) transistor_45 (.in(transistor_46_out), .out(transistor_45_out), .gate(nand_5_out));
  Transistor #(.\type ("n")) transistor_46 (.in(transistor_47_out), .out(transistor_46_out), .gate(nand_6_out));
  Transistor #(.\type ("n")) transistor_47 (.in(transistor_48_out), .out(transistor_47_out), .gate(nand_7_out));
  Transistor #(.\type ("n")) transistor_48 (.in(1'b0), .out(transistor_48_out), .gate(nand_8_out));
  Pull_Resistor #(.pull(1)) pull_resistor_7 (.node(pull_resistor_8_node[1]));
  Transistor #(.\type ("n")) transistor_49 (.in(transistor_50_out), .out(pull_resistor_8_node[1]), .gate(nand_1_out));
  Transistor #(.\type ("n")) transistor_50 (.in(transistor_51_out), .out(transistor_50_out), .gate(nand_2_out));
  Transistor #(.\type ("n")) transistor_51 (.in(transistor_52_out), .out(transistor_51_out), .gate(nand_3_out));
  Transistor #(.\type ("n")) transistor_52 (.in(transistor_53_out), .out(transistor_52_out), .gate(nand_4_out));
  Transistor #(.\type ("n")) transistor_53 (.in(transistor_54_out), .out(transistor_53_out), .gate(nand_5_out));
  Transistor #(.\type ("n")) transistor_54 (.in(transistor_55_out), .out(transistor_54_out), .gate(nand_6_out));
  Transistor #(.\type ("n")) transistor_55 (.in(transistor_56_out), .out(transistor_55_out), .gate(nand_7_out));
  Transistor #(.\type ("n")) transistor_56 (.in(1'b0), .out(transistor_56_out), .gate(nand_8_out));
  Hex_Digit_Display hex_digit_display_1 (.value(rom_1_data_2));  // open: dp
  Hex_Digit_Display hex_digit_display_2 (.value(rom_1_data));  // open: dp
  Pull_Resistor #(.pull(1)) pull_resistor_8 (.node(pull_resistor_8_node[0]));
  Transistor #(.\type ("n")) transistor_57 (.in(transistor_58_out), .out(pull_resistor_8_node[0]), .gate(nand_1_out));
  Transistor #(.\type ("n")) transistor_58 (.in(transistor_59_out), .out(transistor_58_out), .gate(nand_2_out));
  Transistor #(.\type ("n")) transistor_59 (.in(transistor_60_out), .out(transistor_59_out), .gate(nand_3_out));
  Transistor #(.\type ("n")) transistor_60 (.in(transistor_61_out), .out(transistor_60_out), .gate(nand_4_out));
  Transistor #(.\type ("n")) transistor_61 (.in(transistor_62_out), .out(transistor_61_out), .gate(nand_5_out));
  Transistor #(.\type ("n")) transistor_62 (.in(transistor_63_out), .out(transistor_62_out), .gate(nand_6_out));
  Transistor #(.\type ("n")) transistor_63 (.in(transistor_64_out), .out(transistor_63_out), .gate(nand_7_out));
  Transistor #(.\type ("n")) transistor_64 (.in(1'b0), .out(transistor_64_out), .gate(nand_8_out));
  Hex_Digit_Display hex_digit_display_3 (.value(pull_resistor_4_node));  // open: dp
  Hex_Digit_Display hex_digit_display_4 (.value(pull_resistor_8_node));  // open: dp
  _7_Segment_Display u_7_segment_display_1 (
    .g(pull_resistor_4_node[2]), .f(pull_resistor_4_node[1]), .a(pull_resistor_8_node[0]),
    .b(pull_resistor_8_node[1]), .e(pull_resistor_4_node[0]), .d(pull_resistor_8_node[3]),
    .c(pull_resistor_8_node[2]), .dp(pull_resistor_4_node[3]));

  // Notes on the sheet:
  //   Address (Input)
  //   1 of 8 decoder (inverted outputs)
  //   Address (Input)
  //   NAND-type Read-Only Memory (ROM)
  //   contents of rom_1 (hex, n*v repeats v):
  //   8*ff
  //   Memory array
  //   Data (Output)
  //   0
  //   1
  //   2
  //   3
  //   4
  //   5
  //   6
  //   7
  //   Data (Output)
endmodule
