// Logisim project nor_rom.circ as structural Verilog: 1 circuit, main circuit main
module main (
  input  Address__Input,
  input  in_2,
  input  in_3,
  input  in_4,
  input  in_5,
  input  in_6
);

  wire and_1_out, and_2_out, and_3_out, and_4_out, and_5_out, and_6_out, and_7_out, and_8_out, and_9_out,
       and_10_out, and_11_out, and_12_out, not_1_out;
  wire [3:0] pull_resistor_8_node, rom_1_data, rom_1_data_2, transistor_18_out;

  not not_1 (not_1_out, in_3);
  and and_1 (and_1_out, not_1_out, ~in_2);  // AND_Gate
  and and_2 (and_2_out, not_1_out, in_2);
  and and_3 (and_3_out, in_3, ~in_2);  // AND_Gate
  and and_4 (and_4_out, in_3, in_2);
  and and_5 (and_5_out, and_1_out, ~Address__Input);  // AND_Gate
  and and_6 (and_6_out, and_1_out, Address__Input);
  and and_7 (and_7_out, and_2_out, ~Address__Input);  // AND_Gate
  and and_8 (and_8_out, and_2_out, Address__Input);
  and and_9 (and_9_out, and_3_out, ~Address__Input);  // AND_Gate
  and and_10 (and_10_out, and_3_out, Address__Input);
  and and_11 (and_11_out, and_4_out, ~Address__Input);  // AND_Gate
  and and_12 (and_12_out, and_4_out, Address__Input);
  Pull_Resistor #(.pull(1)) pull_resistor_1 (.node(transistor_18_out[3]));
  Transistor #(.\type ("n")) transistor_1 (.in(1'b0), .out(transistor_18_out[3]), .gate(and_5_out));
  Transistor #(.\type ("n")) transistor_2 (.in(1'b0), .out(transistor_18_out[3]), .gate(and_6_out));
  Transistor #(.\type ("n")) transistor_3 (.in(1'b0), .out(transistor_18_out[3]), .gate(and_7_out));
  Transistor #(.\type ("n")) transistor_4 (.in(1'b0), .out(transistor_18_out[3]), .gate(and_8_out));
  Transistor #(.\type ("n")) transistor_5 (.in(1'b0), .out(transistor_18_out[3]), .gate(and_9_out));
  Transistor #(.\type ("n")) transistor_6 (.in(1'b0), .out(transistor_18_out[3]), .gate(and_10_out));
  Transistor #(.\type ("n")) transistor_7 (.in(1'b0), .out(transistor_18_out[3]), .gate(and_11_out));
  Transistor #(.\type ("n")) transistor_8 (.in(1'b0), .out(transistor_18_out[3]), .gate(and_12_out));
  Pull_Resistor #(.pull(1)) pull_resistor_2 (.node(transistor_18_out[2]));
  Transistor #(.\type ("n")) transistor_9 (.in(1'b0), .out(transistor_18_out[2]), .gate(and_5_out));
  Transistor #(.\type ("n")) transistor_10 (.in(1'b0), .out(transistor_18_out[2]), .gate(and_6_out));
  Transistor #(.\type ("n")) transistor_11 (.in(1'b0), .out(transistor_18_out[2]), .gate(and_7_out));
  Transistor #(.\type ("n")) transistor_12 (.in(1'b0), .out(transistor_18_out[2]), .gate(and_8_out));
  Transistor #(.\type ("n")) transistor_13 (.in(1'b0), .out(transistor_18_out[2]), .gate(and_9_out));
  Transistor #(.\type ("n")) transistor_14 (.in(1'b0), .out(transistor_18_out[2]), .gate(and_10_out));
  Transistor #(.\type ("n")) transistor_15 (.in(1'b0), .out(transistor_18_out[2]), .gate(and_11_out));
  Transistor #(.\type ("n")) transistor_16 (.in(1'b0), .out(transistor_18_out[2]), .gate(and_12_out));
  ROM #(.addrWidth(3)) rom_1 (.addr({in_6, in_5, in_4}), .data({rom_1_data_2, rom_1_data}));
  Pull_Resistor #(.pull(1)) pull_resistor_3 (.node(transistor_18_out[1]));
  Transistor #(.\type ("n")) transistor_17 (.in(1'b0), .out(transistor_18_out[1]), .gate(and_5_out));
  Transistor #(.\type ("n")) transistor_18 (.in(1'b0), .out(transistor_18_out[0]), .gate(and_5_out));
  Transistor #(.\type ("n")) transistor_19 (.in(1'b0), .out(transistor_18_out[1]), .gate(and_6_out));
  Transistor #(.\type ("n")) transistor_20 (.in(1'b0), .out(transistor_18_out[0]), .gate(and_6_out));
  Transistor #(.\type ("n")) transistor_21 (.in(1'b0), .out(transistor_18_out[1]), .gate(and_7_out));
  Transistor #(.\type ("n")) transistor_22 (.in(1'b0), .out(transistor_18_out[0]), .gate(and_7_out));
  Transistor #(.\type ("n")) transistor_23 (.in(1'b0), .out(transistor_18_out[1]), .gate(and_8_out));
  Transistor #(.\type ("n")) transistor_24 (.in(1'b0), .out(transistor_18_out[0]), .gate(and_8_out));
  Transistor #(.\type ("n")) transistor_25 (.in(1'b0), .out(transistor_18_out[1]), .gate(and_9_out));
  Transistor #(.\type ("n")) transistor_26 (.in(1'b0), .out(transistor_18_out[0]), .gate(and_9_out));
  Transistor #(.\type ("n")) transistor_27 (.in(1'b0), .out(transistor_18_out[1]), .gate(and_10_out));
  Transistor #(.\type ("n")) transistor_28 (.in(1'b0), .out(transistor_18_out[0]), .gate(and_10_out));
  Transistor #(.\type ("n")) transistor_29 (.in(1'b0), .out(transistor_18_out[1]), .gate(and_11_out));
  Transistor #(.\type ("n")) transistor_30 (.in(1'b0), .out(transistor_18_out[0]), .gate(and_11_out));
  Transistor #(.\type ("n")) transistor_31 (.in(1'b0), .out(transistor_18_out[1]), .gate(and_12_out));
  Transistor #(.\type ("n")) transistor_32 (.in(1'b0), .out(transistor_18_out[0]), .gate(and_12_out));
  Pull_Resistor #(.pull(1)) pull_resistor_4 (.node(transistor_18_out[0]));
  Transistor #(.\type ("n")) transistor_33 (.in(1'b0), .out(pull_resistor_8_node[3]), .gate(and_5_out));
  Transistor #(.\type ("n")) transistor_34 (.in(1'b0), .out(pull_resistor_8_node[3]), .gate(and_6_out));
  Transistor #(.\type ("n")) transistor_35 (.in(1'b0), .out(pull_resistor_8_node[3]), .gate(and_7_out));
  Transistor #(.\type ("n")) transistor_36 (.in(1'b0), .out(pull_resistor_8_node[3]), .gate(and_8_out));
  Transistor #(.\type ("n")) transistor_37 (.in(1'b0), .out(pull_resistor_8_node[3]), .gate(and_9_out));
  Transistor #(.\type ("n")) transistor_38 (.in(1'b0), .out(pull_resistor_8_node[3]), .gate(and_10_out));
  Transistor #(.\type ("n")) transistor_39 (.in(1'b0), .out(pull_resistor_8_node[3]), .gate(and_11_out));
  Transistor #(.\type ("n")) transistor_40 (.in(1'b0), .out(pull_resistor_8_node[3]), .gate(and_12_out));
  Pull_Resistor #(.pull(1)) pull_resistor_5 (.node(pull_resistor_8_node[3]));
  Pull_Resistor #(.pull(1)) pull_resistor_6 (.node(pull_resistor_8_node[2]));
  Transistor #(.\type ("n")) transistor_41 (.in(1'b0), .out(pull_resistor_8_node[2]), .gate(and_5_out));
  Transistor #(.\type ("n")) transistor_42 (.in(1'b0), .out(pull_resistor_8_node[2]), .gate(and_6_out));
  Transistor #(.\type ("n")) transistor_43 (.in(1'b0), .out(pull_resistor_8_node[2]), .gate(and_7_out));
  Transistor #(.\type ("n")) transistor_44 (.in(1'b0), .out(pull_resistor_8_node[2]), .gate(and_8_out));
  Transistor #(.\type ("n")) transistor_45 (.in(1'b0), .out(pull_resistor_8_node[2]), .gate(and_9_out));
  Transistor #(.\type ("n")) transistor_46 (.in(1'b0), .out(pull_resistor_8_node[2]), .gate(and_10_out));
  Transistor #(.\type ("n")) transistor_47 (.in(1'b0), .out(pull_resistor_8_node[2]), .gate(and_11_out));
  Transistor #(.\type ("n")) transistor_48 (.in(1'b0), .out(pull_resistor_8_node[2]), .gate(and_12_out));
  Pull_Resistor #(.pull(1)) pull_resistor_7 (.node(pull_resistor_8_node[1]));
  Transistor #(.\type ("n")) transistor_49 (.in(1'b0), .out(pull_resistor_8_node[1]), .gate(and_5_out));
  Transistor #(.\type ("n")) transistor_50 (.in(1'b0), .out(pull_resistor_8_node[1]), .gate(and_6_out));
  Transistor #(.\type ("n")) transistor_51 (.in(1'b0), .out(pull_resistor_8_node[1]), .gate(and_7_out));
  Transistor #(.\type ("n")) transistor_52 (.in(1'b0), .out(pull_resistor_8_node[1]), .gate(and_8_out));
  Transistor #(.\type ("n")) transistor_53 (.in(1'b0), .out(pull_resistor_8_node[1]), .gate(and_9_out));
  Transistor #(.\type ("n")) transistor_54 (.in(1'b0), .out(pull_resistor_8_node[1]), .gate(and_10_out));
  Transistor #(.\type ("n")) transistor_55 (.in(1'b0), .out(pull_resistor_8_node[1]), .gate(and_11_out));
  Transistor #(.\type ("n")) transistor_56 (.in(1'b0), .out(pull_resistor_8_node[1]), .gate(and_12_out));
  Hex_Digit_Display hex_digit_display_1 (.value(rom_1_data_2));  // open: dp
  Pull_Resistor #(.pull(1)) pull_resistor_8 (.node(pull_resistor_8_node[0]));
  Transistor #(.\type ("n")) transistor_57 (.in(1'b0), .out(pull_resistor_8_node[0]), .gate(and_5_out));
  Transistor #(.\type ("n")) transistor_58 (.in(1'b0), .out(pull_resistor_8_node[0]), .gate(and_6_out));
  Transistor #(.\type ("n")) transistor_59 (.in(1'b0), .out(pull_resistor_8_node[0]), .gate(and_7_out));
  Transistor #(.\type ("n")) transistor_60 (.in(1'b0), .out(pull_resistor_8_node[0]), .gate(and_8_out));
  Transistor #(.\type ("n")) transistor_61 (.in(1'b0), .out(pull_resistor_8_node[0]), .gate(and_9_out));
  Transistor #(.\type ("n")) transistor_62 (.in(1'b0), .out(pull_resistor_8_node[0]), .gate(and_10_out));
  Transistor #(.\type ("n")) transistor_63 (.in(1'b0), .out(pull_resistor_8_node[0]), .gate(and_11_out));
  Transistor #(.\type ("n")) transistor_64 (.in(1'b0), .out(pull_resistor_8_node[0]), .gate(and_12_out));
  Hex_Digit_Display hex_digit_display_2 (.value(rom_1_data));  // open: dp
  Hex_Digit_Display hex_digit_display_3 (.value(transistor_18_out));  // open: dp
  Hex_Digit_Display hex_digit_display_4 (.value(pull_resistor_8_node));  // open: dp

  // Notes on the sheet:
  //   3 to 8 decoder
  //   Address (Input)
  //   NOR-type Read-Only Memory (ROM)
  //   Memory array
  //   Data (Output)
  //   0
  //   1
  //   2
  //   3
  //   4
  //   5
  //   6
  //   7
  //   Data (Output)
endmodule
