// Logisim project ram_idea.circ as structural Verilog: 3 circuits, main circuit main
module main (
  input  Address__Input,
  input  in_2,
  input  in_3,
  input  Write_Enable,
  input  Data__Input,
  input  in_6,
  input  in_7,
  input  in_8,
  input  in_9,
  input  in_10,
  input  in_11,
  input  in_12,
  input  in_13,
  input  in_14,
  input  in_15,
  input  in_16,
  input  in_17,
  input  in_18,
  input  in_19,
  input  in_20,
  input  in_21,
  input  in_22,
  input  in_23,
  input  in_24
);

  wire and_1_out, and_2_out, and_3_out, and_4_out, and_5_out, and_6_out, and_7_out, and_8_out, and_9_out,
       and_10_out, and_11_out, and_12_out, clock_1_out, clock_2_out, input_d_latch_1_q, input_d_latch_2_q,
       input_d_latch_3_q, input_d_latch_4_q, input_d_latch_5_q, input_d_latch_6_q, input_d_latch_7_q,
       input_d_latch_8_q, nand_1_out, not_1_out, not_2_out;
  wire [3:0] pull_resistor_4_node, pull_resistor_8_node, ram_1_dout, ram_1_dout_2;

  Clock clock_1 (.out(clock_1_out));
  not not_1 (not_1_out, in_3);
  nand nand_1 (nand_1_out, Write_Enable, clock_1_out);
  input_D_latch input_d_latch_1 (.D(Data__Input), .E(nand_1_out), .Q(input_d_latch_1_q));
  input_D_latch input_d_latch_2 (.D(in_6), .E(nand_1_out), .Q(input_d_latch_2_q));
  input_D_latch input_d_latch_3 (.D(in_7), .E(nand_1_out), .Q(input_d_latch_3_q));
  input_D_latch input_d_latch_4 (.D(in_8), .E(nand_1_out), .Q(input_d_latch_4_q));
  input_D_latch input_d_latch_5 (.D(in_9), .E(nand_1_out), .Q(input_d_latch_5_q));
  input_D_latch input_d_latch_6 (.D(in_10), .E(nand_1_out), .Q(input_d_latch_6_q));
  input_D_latch input_d_latch_7 (.D(in_11), .E(nand_1_out), .Q(input_d_latch_7_q));
  input_D_latch input_d_latch_8 (.D(in_12), .E(nand_1_out), .Q(input_d_latch_8_q));
  Clock clock_2 (.out(clock_2_out));
  and and_1 (and_1_out, not_1_out, ~in_2);  // AND_Gate
  and and_2 (and_2_out, not_1_out, in_2);
  and and_3 (and_3_out, in_3, ~in_2);  // AND_Gate
  and and_4 (and_4_out, in_3, in_2);
  not not_2 (not_2_out, nand_1_out);
  and and_5 (and_5_out, and_1_out, ~Address__Input);  // AND_Gate
  and and_6 (and_6_out, and_1_out, Address__Input);
  and and_7 (and_7_out, and_2_out, ~Address__Input);  // AND_Gate
  and and_8 (and_8_out, and_2_out, Address__Input);
  and and_9 (and_9_out, and_3_out, ~Address__Input);  // AND_Gate
  and and_10 (and_10_out, and_3_out, Address__Input);
  and and_11 (and_11_out, and_4_out, ~Address__Input);  // AND_Gate
  and and_12 (and_12_out, and_4_out, Address__Input);
  Pull_Resistor #(.pull(1)) pull_resistor_1 (.node(pull_resistor_4_node[3]));
  D_latch_with_activation d_latch_with_activation_1 (
    .D(input_d_latch_8_q), .Write_Data(not_2_out), .Activate(and_5_out), .Q(pull_resistor_4_node[3]));
  D_latch_with_activation d_latch_with_activation_2 (
    .D(input_d_latch_8_q), .Write_Data(not_2_out), .Activate(and_6_out), .Q(pull_resistor_4_node[3]));
  D_latch_with_activation d_latch_with_activation_3 (
    .D(input_d_latch_8_q), .Write_Data(not_2_out), .Activate(and_7_out), .Q(pull_resistor_4_node[3]));
  D_latch_with_activation d_latch_with_activation_4 (
    .D(input_d_latch_8_q), .Write_Data(not_2_out), .Activate(and_8_out), .Q(pull_resistor_4_node[3]));
  D_latch_with_activation d_latch_with_activation_5 (
    .D(input_d_latch_8_q), .Write_Data(not_2_out), .Activate(and_9_out), .Q(pull_resistor_4_node[3]));
  D_latch_with_activation d_latch_with_activation_6 (
    .D(input_d_latch_8_q), .Write_Data(not_2_out), .Activate(and_10_out), .Q(pull_resistor_4_node[3]));
  D_latch_with_activation d_latch_with_activation_7 (
    .D(input_d_latch_8_q), .Write_Data(not_2_out), .Activate(and_11_out), .Q(pull_resistor_4_node[3]));
  D_latch_with_activation d_latch_with_activation_8 (
    .D(input_d_latch_8_q), .Write_Data(not_2_out), .Activate(and_12_out), .Q(pull_resistor_4_node[3]));
  RAM #(.addrWidth(3), .asyncread("true")) ram_1 (
    .addr({in_15, in_14, in_13}), .we(in_16), .clk(clock_2_out),
    .din({in_24, in_23, in_22, in_21, in_20, in_19, in_18, in_17}), .dout({ram_1_dout_2, ram_1_dout}));  // open: oe
  Pull_Resistor #(.pull(1)) pull_resistor_2 (.node(pull_resistor_4_node[2]));
  D_latch_with_activation d_latch_with_activation_9 (
    .D(input_d_latch_7_q), .Write_Data(not_2_out), .Activate(and_5_out), .Q(pull_resistor_4_node[2]));
  D_latch_with_activation d_latch_with_activation_10 (
    .D(input_d_latch_7_q), .Write_Data(not_2_out), .Activate(and_6_out), .Q(pull_resistor_4_node[2]));
  D_latch_with_activation d_latch_with_activation_11 (
    .D(input_d_latch_7_q), .Write_Data(not_2_out), .Activate(and_7_out), .Q(pull_resistor_4_node[2]));
  D_latch_with_activation d_latch_with_activation_12 (
    .D(input_d_latch_7_q), .Write_Data(not_2_out), .Activate(and_8_out), .Q(pull_resistor_4_node[2]));
  D_latch_with_activation d_latch_with_activation_13 (
    .D(input_d_latch_7_q), .Write_Data(not_2_out), .Activate(and_9_out), .Q(pull_resistor_4_node[2]));
  D_latch_with_activation d_latch_with_activation_14 (
    .D(input_d_latch_7_q), .Write_Data(not_2_out), .Activate(and_10_out), .Q(pull_resistor_4_node[2]));
  D_latch_with_activation d_latch_with_activation_15 (
    .D(input_d_latch_7_q), .Write_Data(not_2_out), .Activate(and_11_out), .Q(pull_resistor_4_node[2]));
  D_latch_with_activation d_latch_with_activation_16 (
    .D(input_d_latch_7_q), .Write_Data(not_2_out), .Activate(and_12_out), .Q(pull_resistor_4_node[2]));
  Pull_Resistor #(.pull(1)) pull_resistor_3 (.node(pull_resistor_4_node[1]));
  D_latch_with_activation d_latch_with_activation_17 (
    .D(input_d_latch_6_q), .Write_Data(not_2_out), .Activate(and_5_out), .Q(pull_resistor_4_node[1]));
  D_latch_with_activation d_latch_with_activation_18 (
    .D(input_d_latch_6_q), .Write_Data(not_2_out), .Activate(and_6_out), .Q(pull_resistor_4_node[1]));
  D_latch_with_activation d_latch_with_activation_19 (
    .D(input_d_latch_6_q), .Write_Data(not_2_out), .Activate(and_7_out), .Q(pull_resistor_4_node[1]));
  D_latch_with_activation d_latch_with_activation_20 (
    .D(input_d_latch_6_q), .Write_Data(not_2_out), .Activate(and_8_out), .Q(pull_resistor_4_node[1]));
  D_latch_with_activation d_latch_with_activation_21 (
    .D(input_d_latch_6_q), .Write_Data(not_2_out), .Activate(and_9_out), .Q(pull_resistor_4_node[1]));
  D_latch_with_activation d_latch_with_activation_22 (
    .D(input_d_latch_6_q), .Write_Data(not_2_out), .Activate(and_10_out), .Q(pull_resistor_4_node[1]));
  D_latch_with_activation d_latch_with_activation_23 (
    .D(input_d_latch_6_q), .Write_Data(not_2_out), .Activate(and_11_out), .Q(pull_resistor_4_node[1]));
  D_latch_with_activation d_latch_with_activation_24 (
    .D(input_d_latch_6_q), .Write_Data(not_2_out), .Activate(and_12_out), .Q(pull_resistor_4_node[1]));
  Pull_Resistor #(.pull(1)) pull_resistor_4 (.node(pull_resistor_4_node[0]));
  D_latch_with_activation d_latch_with_activation_25 (
    .D(input_d_latch_5_q), .Write_Data(not_2_out), .Activate(and_5_out), .Q(pull_resistor_4_node[0]));
  D_latch_with_activation d_latch_with_activation_26 (
    .D(input_d_latch_4_q), .Write_Data(not_2_out), .Activate(and_5_out), .Q(pull_resistor_8_node[3]));
  D_latch_with_activation d_latch_with_activation_27 (
    .D(input_d_latch_5_q), .Write_Data(not_2_out), .Activate(and_6_out), .Q(pull_resistor_4_node[0]));
  D_latch_with_activation d_latch_with_activation_28 (
    .D(input_d_latch_4_q), .Write_Data(not_2_out), .Activate(and_6_out), .Q(pull_resistor_8_node[3]));
  D_latch_with_activation d_latch_with_activation_29 (
    .D(input_d_latch_5_q), .Write_Data(not_2_out), .Activate(and_7_out), .Q(pull_resistor_4_node[0]));
  D_latch_with_activation d_latch_with_activation_30 (
    .D(input_d_latch_4_q), .Write_Data(not_2_out), .Activate(and_7_out), .Q(pull_resistor_8_node[3]));
  D_latch_with_activation d_latch_with_activation_31 (
    .D(input_d_latch_5_q), .Write_Data(not_2_out), .Activate(and_8_out), .Q(pull_resistor_4_node[0]));
  D_latch_with_activation d_latch_with_activation_32 (
    .D(input_d_latch_4_q), .Write_Data(not_2_out), .Activate(and_8_out), .Q(pull_resistor_8_node[3]));
  D_latch_with_activation d_latch_with_activation_33 (
    .D(input_d_latch_5_q), .Write_Data(not_2_out), .Activate(and_9_out), .Q(pull_resistor_4_node[0]));
  D_latch_with_activation d_latch_with_activation_34 (
    .D(input_d_latch_4_q), .Write_Data(not_2_out), .Activate(and_9_out), .Q(pull_resistor_8_node[3]));
  D_latch_with_activation d_latch_with_activation_35 (
    .D(input_d_latch_5_q), .Write_Data(not_2_out), .Activate(and_10_out), .Q(pull_resistor_4_node[0]));
  D_latch_with_activation d_latch_with_activation_36 (
    .D(input_d_latch_4_q), .Write_Data(not_2_out), .Activate(and_10_out), .Q(pull_resistor_8_node[3]));
  D_latch_with_activation d_latch_with_activation_37 (
    .D(input_d_latch_5_q), .Write_Data(not_2_out), .Activate(and_11_out), .Q(pull_resistor_4_node[0]));
  D_latch_with_activation d_latch_with_activation_38 (
    .D(input_d_latch_4_q), .Write_Data(not_2_out), .Activate(and_11_out), .Q(pull_resistor_8_node[3]));
  D_latch_with_activation d_latch_with_activation_39 (
    .D(input_d_latch_5_q), .Write_Data(not_2_out), .Activate(and_12_out), .Q(pull_resistor_4_node[0]));
  D_latch_with_activation d_latch_with_activation_40 (
    .D(input_d_latch_4_q), .Write_Data(not_2_out), .Activate(and_12_out), .Q(pull_resistor_8_node[3]));
  Pull_Resistor #(.pull(1)) pull_resistor_5 (.node(pull_resistor_8_node[3]));
  Pull_Resistor #(.pull(1)) pull_resistor_6 (.node(pull_resistor_8_node[2]));
  D_latch_with_activation d_latch_with_activation_41 (
    .D(input_d_latch_3_q), .Write_Data(not_2_out), .Activate(and_5_out), .Q(pull_resistor_8_node[2]));
  D_latch_with_activation d_latch_with_activation_42 (
    .D(input_d_latch_3_q), .Write_Data(not_2_out), .Activate(and_6_out), .Q(pull_resistor_8_node[2]));
  D_latch_with_activation d_latch_with_activation_43 (
    .D(input_d_latch_3_q), .Write_Data(not_2_out), .Activate(and_7_out), .Q(pull_resistor_8_node[2]));
  D_latch_with_activation d_latch_with_activation_44 (
    .D(input_d_latch_3_q), .Write_Data(not_2_out), .Activate(and_8_out), .Q(pull_resistor_8_node[2]));
  D_latch_with_activation d_latch_with_activation_45 (
    .D(input_d_latch_3_q), .Write_Data(not_2_out), .Activate(and_9_out), .Q(pull_resistor_8_node[2]));
  D_latch_with_activation d_latch_with_activation_46 (
    .D(input_d_latch_3_q), .Write_Data(not_2_out), .Activate(and_10_out), .Q(pull_resistor_8_node[2]));
  D_latch_with_activation d_latch_with_activation_47 (
    .D(input_d_latch_3_q), .Write_Data(not_2_out), .Activate(and_11_out), .Q(pull_resistor_8_node[2]));
  D_latch_with_activation d_latch_with_activation_48 (
    .D(input_d_latch_3_q), .Write_Data(not_2_out), .Activate(and_12_out), .Q(pull_resistor_8_node[2]));
  Hex_Digit_Display hex_digit_display_1 (.value(ram_1_dout_2));  // open: dp
  Pull_Resistor #(.pull(1)) pull_resistor_7 (.node(pull_resistor_8_node[1]));
  D_latch_with_activation d_latch_with_activation_49 (
    .D(input_d_latch_2_q), .Write_Data(not_2_out), .Activate(and_5_out), .Q(pull_resistor_8_node[1]));
  D_latch_with_activation d_latch_with_activation_50 (
    .D(input_d_latch_2_q), .Write_Data(not_2_out), .Activate(and_6_out), .Q(pull_resistor_8_node[1]));
  D_latch_with_activation d_latch_with_activation_51 (
    .D(input_d_latch_2_q), .Write_Data(not_2_out), .Activate(and_7_out), .Q(pull_resistor_8_node[1]));
  D_latch_with_activation d_latch_with_activation_52 (
    .D(input_d_latch_2_q), .Write_Data(not_2_out), .Activate(and_8_out), .Q(pull_resistor_8_node[1]));
  D_latch_with_activation d_latch_with_activation_53 (
    .D(input_d_latch_2_q), .Write_Data(not_2_out), .Activate(and_9_out), .Q(pull_resistor_8_node[1]));
  D_latch_with_activation d_latch_with_activation_54 (
    .D(input_d_latch_2_q), .Write_Data(not_2_out), .Activate(and_10_out), .Q(pull_resistor_8_node[1]));
  D_latch_with_activation d_latch_with_activation_55 (
    .D(input_d_latch_2_q), .Write_Data(not_2_out), .Activate(and_11_out), .Q(pull_resistor_8_node[1]));
  D_latch_with_activation d_latch_with_activation_56 (
    .D(input_d_latch_2_q), .Write_Data(not_2_out), .Activate(and_12_out), .Q(pull_resistor_8_node[1]));
  Hex_Digit_Display hex_digit_display_2 (.value(ram_1_dout));  // open: dp
  Pull_Resistor #(.pull(1)) pull_resistor_8 (.node(pull_resistor_8_node[0]));
  D_latch_with_activation d_latch_with_activation_57 (
    .D(input_d_latch_1_q), .Write_Data(not_2_out), .Activate(and_5_out), .Q(pull_resistor_8_node[0]));
  D_latch_with_activation d_latch_with_activation_58 (
    .D(input_d_latch_1_q), .Write_Data(not_2_out), .Activate(and_6_out), .Q(pull_resistor_8_node[0]));
  D_latch_with_activation d_latch_with_activation_59 (
    .D(input_d_latch_1_q), .Write_Data(not_2_out), .Activate(and_7_out), .Q(pull_resistor_8_node[0]));
  D_latch_with_activation d_latch_with_activation_60 (
    .D(input_d_latch_1_q), .Write_Data(not_2_out), .Activate(and_8_out), .Q(pull_resistor_8_node[0]));
  D_latch_with_activation d_latch_with_activation_61 (
    .D(input_d_latch_1_q), .Write_Data(not_2_out), .Activate(and_9_out), .Q(pull_resistor_8_node[0]));
  D_latch_with_activation d_latch_with_activation_62 (
    .D(input_d_latch_1_q), .Write_Data(not_2_out), .Activate(and_10_out), .Q(pull_resistor_8_node[0]));
  D_latch_with_activation d_latch_with_activation_63 (
    .D(input_d_latch_1_q), .Write_Data(not_2_out), .Activate(and_11_out), .Q(pull_resistor_8_node[0]));
  D_latch_with_activation d_latch_with_activation_64 (
    .D(input_d_latch_1_q), .Write_Data(not_2_out), .Activate(and_12_out), .Q(pull_resistor_8_node[0]));
  LED led_1 (.in(ram_1_dout_2[1]));
  LED led_2 (.in(ram_1_dout_2[0]));
  LED led_3 (.in(ram_1_dout_2[3]));
  LED led_4 (.in(ram_1_dout_2[2]));
  Hex_Digit_Display hex_digit_display_3 (.value(pull_resistor_4_node));  // open: dp
  LED led_5 (.in(ram_1_dout[3]));
  LED led_6 (.in(ram_1_dout[2]));
  LED led_7 (.in(ram_1_dout[1]));
  LED led_8 (.in(ram_1_dout[0]));
  Hex_Digit_Display hex_digit_display_4 (.value(pull_resistor_8_node));  // open: dp
  LED led_9 (.in(pull_resistor_4_node[3]));
  LED led_10 (.in(pull_resistor_4_node[2]));
  LED led_11 (.in(pull_resistor_4_node[1]));
  LED led_12 (.in(pull_resistor_4_node[0]));
  LED led_13 (.in(pull_resistor_8_node[3]));
  LED led_14 (.in(pull_resistor_8_node[2]));
  LED led_15 (.in(pull_resistor_8_node[1]));
  LED led_16 (.in(pull_resistor_8_node[0]));

  // Notes on the sheet:
  //   CLK
  //   Address (Input)
  //   Write Enable
  //   Data (Input)
  //   CLK
  //   Random Access Memory (RAM)
  //   Data (Output)
  //   Data (Output)
endmodule

module D_latch_with_activation (
  input  D,
  input  Write_Data,
  input  Activate,
  output Q
);

  wire and_1_out, and_2_out, nand_1_out, nand_2_out, nand_3_out, nand_4_out;

  and and_1 (and_1_out, Write_Data, Activate);
  nand nand_1 (nand_1_out, D, and_1_out);
  nand nand_2 (nand_2_out, nand_1_out, and_1_out);
  nand nand_3 (nand_3_out, nand_1_out, nand_4_out);
  nand nand_4 (nand_4_out, nand_3_out, nand_2_out);
  Transistor #(.\type ("n")) transistor_1 (.in(1'b0), .out(Q), .gate(and_2_out));
  and and_2 (and_2_out, nand_4_out, Activate);

  // Notes on the sheet:
  //   Activation signal outputs the data stored in the memory cell onto the bit line
  //   It also allows Write_Data signal to change value stored in the cell to the value supplied on input D
  //   PS: Logisim is not powerful enough to simulate real latch circuit used in RAM ICs
  //   I am using a D latch in its place for the lack of a better option! :)
  //   Observe that the initial value of the latch is shown in red, it means that logisim is unable
  //   to determine it. This is true to reality, because physical RAM content appears random on power up
  //   it is up to the software to initialise it. In Logisim, however, RAM is always filled with 0s :(
endmodule

module input_D_latch (
  input  D,
  input  E,
  output Q
);

  wire nand_1_out, nand_2_out, nand_4_out;

  nand nand_1 (nand_1_out, D, E);
  nand nand_2 (nand_2_out, nand_1_out, E);
  nand nand_3 (Q, nand_1_out, nand_4_out);
  nand nand_4 (nand_4_out, Q, nand_2_out);
endmodule
