// Logisim project simple_alu.circ as structural Verilog: 1 circuit, main circuit main
module main (
);

  wire [1:0] dipswitch_3_sw2;
  wire [3:0] adder_1_out, dipswitch_1_sw4, dipswitch_2_sw4, divider_1_out, multiplexer_1_out,
       multiplier_1_out, subtractor_1_out;

  DipSwitch #(.number(4)) dipswitch_1 (
    .sw1(dipswitch_1_sw4[3]), .sw2(dipswitch_1_sw4[2]), .sw3(dipswitch_1_sw4[1]), .sw4(dipswitch_1_sw4[0]));
  DipSwitch #(.number(4)) dipswitch_2 (
    .sw1(dipswitch_2_sw4[3]), .sw2(dipswitch_2_sw4[2]), .sw3(dipswitch_2_sw4[1]), .sw4(dipswitch_2_sw4[0]));
  Adder #(.width(4)) adder_1 (.a(dipswitch_1_sw4), .b(dipswitch_2_sw4), .out(adder_1_out));  // open: cin, cout
  Subtractor #(.width(4)) subtractor_1 (
    .a(dipswitch_1_sw4), .b(dipswitch_2_sw4), .out(subtractor_1_out));  // open: bin, bout
  Multiplier #(.width(4)) multiplier_1 (
    .a(dipswitch_1_sw4), .b(dipswitch_2_sw4), .out(multiplier_1_out));  // open: cin, cout
  Divider #(.width(4)) divider_1 (.a(dipswitch_1_sw4), .b(dipswitch_2_sw4), .out(divider_1_out));  // open: upper, rem
  Multiplexer #(.select(2), .width(4)) multiplexer_1 (
    .in0(adder_1_out), .in1(subtractor_1_out), .in2(multiplier_1_out), .in3(divider_1_out),
    .out(multiplexer_1_out), .sel(dipswitch_3_sw2));
  DipSwitch #(.number(2)) dipswitch_3 (.sw1(dipswitch_3_sw2[1]), .sw2(dipswitch_3_sw2[0]));
  LedBar #(.matrixcols(4)) ledbar_1 (
    .led0(multiplexer_1_out[3]), .led1(multiplexer_1_out[2]), .led2(multiplexer_1_out[1]),
    .led3(multiplexer_1_out[0]));

  // Notes on the sheet:
  //   X
  //   Y
  //   00: Add
  //   01: Subtract
  //   10: Multiply
  //   11: Divide
endmodule
